# Fritzing sketch Controlling 2 servo motors (saved by Fritzing 0.9.4)

parts:
  Parça1 = Arduino Uno (Rev3)
  J1 = Basic Servo
  J2 = Basic Servo
  Power_plug1 = Power plug

nets:
  N1: Parça1.D6_PWM, J2.pulse
  N2: Parça1.D7, J1.pulse
  GND: Parça1.GND, J1.gnd, J2.gnd, Power_plug1.GND
  VCC: J1.vcc, J2.vcc, Power_plug1.VCC

notes:
  6 Volts

// code stored in the sketch: Ultrosinik_servo.ino
#define trigPin 6
#define echoPin 5
#include <Servo.h>
int aci;

Servo myservo;  // create servo object to control a servo
// twelve servo objects can be created on most boards
    

void setup() {
  myservo.attach(9);
  Serial.begin (9600);
  pinMode(trigPin, OUTPUT);
  pinMode(echoPin, INPUT);// attaches the servo on pin 9 to the servo object
}
void loop() {
  int sure, mesafe;
  digitalWrite(trigPin, HIGH);
  delayMicroseconds(1000);
  digitalWrite(trigPin, LOW);
  sure = pulseIn(echoPin, HIGH);
  mesafe = sure/58; // neden 58 acaba :)
  if (mesafe >= 50 || mesafe <= 0){
    Serial.println("Güvenli bölge");
  
  }  else{
    Serial.print(mesafe);
    Serial.println(" cm");
    myservo.write(90);
    delay(400);
    for(aci=90;aci>=0;aci-=10)
      myservo.write(aci);
      delay(100); 
}// tell servo to go to position in variable 'pos'
                          // waits 15ms for the servo to reach the position
  
  delay(600);
  }
